// Logisim project logisim-mp3-player.circ as structural Verilog: 6 circuits, main circuit main
module main (
  input  on_off
);

  wire button_1_out, decoder_1_out0, decoder_1_out1, decoder_1_out2, decoder_1_out3, listen_out,
       next_song_out, not_1_out, not_2_out, not_3_out, not_4_out, previous_song_out,
       recoding_1_mode_listening, recoding_1_mode_recoding, start_recoding_out, t_ff_1_q, t_ff_2_q, t_ff_3_q,
       t_ff_4_q;
  wire [1:0] led_display_1_track_num;
  wire [6:0] led_display_1_line1, led_display_1_line2, led_display_1_line3, led_display_1_line4,
       led_display_1_line5;
  wire [7:0] mckeyboard_1_p1, recoding_1_out_6, soundtrack1_1_out_3, soundtrack2_1_out_3, soundtrack3_1_out_3;

  LED led_1 (.in(on_off));
  Button previous_song (.out(previous_song_out));
  Button next_song (.out(next_song_out));
  Button button_1 (.out(button_1_out));
  Button start_recoding (.out(start_recoding_out));
  Button listen (.out(listen_out));
  LED R (.in(recoding_1_mode_recoding));
  LED L (.in(recoding_1_mode_listening));
  led_display led_display_1 (
    .onoff(on_off), .previous_song(previous_song_out), .next_song(next_song_out),
    .line1(led_display_1_line1), .line2(led_display_1_line2), .line3(led_display_1_line3),
    .line4(led_display_1_line4), .line5(led_display_1_line5), .track_num(led_display_1_track_num));
  // MCKeyboard mckeyboard_1: pin names not known; wires that end beside it: mckeyboard_1_p1
  DotMatrix dotmatrix_1 (
    .col0(led_display_1_line1), .col1(led_display_1_line2), .col2(led_display_1_line3),
    .col3(led_display_1_line4), .col4(led_display_1_line5));
  Decoder #(.select(2)) decoder_1 (
    .out0(decoder_1_out0), .out1(decoder_1_out1), .out2(decoder_1_out2), .out3(decoder_1_out3),
    .sel(led_display_1_track_num), .en(on_off));
  T_Flip_Flop t_ff_1 (.T(decoder_1_out0), .clk(button_1_out), .Q(t_ff_1_q));  // open: Qn, reset, preset
  not not_1 (not_1_out, decoder_1_out0);
  T_Flip_Flop t_ff_2 (.T(decoder_1_out1), .clk(button_1_out), .Q(t_ff_2_q));  // open: Qn, reset, preset
  not not_2 (not_2_out, decoder_1_out1);
  T_Flip_Flop t_ff_3 (.T(decoder_1_out2), .clk(button_1_out), .Q(t_ff_3_q));  // open: Qn, reset, preset
  not not_3 (not_3_out, decoder_1_out2);
  T_Flip_Flop t_ff_4 (.T(decoder_1_out3), .clk(button_1_out), .Q(t_ff_4_q));  // open: Qn, reset, preset
  not not_4 (not_4_out, decoder_1_out3);
  soundTrack1 soundtrack1_1 (.Stop(t_ff_1_q), .reset(not_1_out), .out_3(soundtrack1_1_out_3));
  soundTrack2 soundtrack2_1 (.Stop(t_ff_2_q), .reset(not_2_out), .out_3(soundtrack2_1_out_3));
  soundTrack3 soundtrack3_1 (.stop(t_ff_3_q), .reset(not_3_out), .out_3(soundtrack3_1_out_3));
  recoding recoding_1 (
    .reset(not_4_out), .stop(t_ff_4_q), .start_recoding(start_recoding_out), .listen(listen_out),
    .piano(mckeyboard_1_p1), .out_6(recoding_1_out_6), .mode_listening(recoding_1_mode_listening),
    .mode_recoding(recoding_1_mode_recoding));
  // sound_emitter sound_emitter_1: pin names not known; wires that end beside it: soundtrack1_1_out_3
  // sound_emitter sound_emitter_2: pin names not known; wires that end beside it: soundtrack2_1_out_3
  // sound_emitter sound_emitter_3: pin names not known; wires that end beside it: soundtrack3_1_out_3
  // sound_emitter sound_emitter_4: pin names not known; wires that end beside it: recoding_1_out_6
  // sound_emitter sound_emitter_5: pin names not known; wires that end beside it: mckeyboard_1_p1

  // Notes on the sheet:
  //   play / stop
  //   R : recoding mode
  //   L : listening mode
  //   Track
  //   추억의 MP3 Player
  //   ㄴ Track1: 윤도현 - 사랑했나봐
  //   ㄴ Track3: 박효신 - 눈의 꽃
  //   ㄴ Track4: Recoding mode
  //   ㄴ Track2: 체리필터 - 낭만고양이
  //   * 아래의 피아노를 쳐서 노래를 녹음할 수 있어요
endmodule

module led_display (
  input  onoff,
  input  previous_song,
  input  next_song,
  output [6:0] line1,
  output [6:0] line2,
  output [6:0] line3,
  output [6:0] line4,
  output [6:0] line5,
  output [1:0] track_num
);

  wire or_1_out;
  wire [6:0] pla_1_out, pla_2_out, pla_3_out, pla_4_out, pla_5_out;
  wire [34:0] bit_extender_1_out;

  Counter #(.max('h3), .width(2)) counter_1 (
    .Q(track_num), .up(next_song), .clk(or_1_out));  // open: load, D, count, carry, clr
  or or_1 (or_1_out, previous_song, next_song);
  PLA #(.out_width(7), .\table ("00 0000000 # 1\n01 1000011 # 2\n10 1000001 # 3\n11 0001100 # 4")) pla_1 (
    .in(track_num), .out(pla_1_out));
  PLA #(.out_width(7), .\table ("00 0100001 # 1\n01 1000101 # 2\n10 1001001 # 3\n11 0010100 # 4")) pla_2 (
    .in(track_num), .out(pla_2_out));
  PLA #(.out_width(7), .\table ("00 1111111 # 1\n01 1001001 # 2\n10 1001001 # 3\n11 0100100 # 4")) pla_3 (
    .in(track_num), .out(pla_3_out));
  PLA #(.out_width(7), .\table ("00 0000001 # 1\n01 1001001 # 2\n10 1001001 # 3\n11 1111111 # 4")) pla_4 (
    .in(track_num), .out(pla_4_out));
  PLA #(.out_width(7), .\table ("00 0000000 # 1\n01 0110001 # 2\n10 0110110 # 3\n11 0000100 # 4")) pla_5 (
    .in(track_num), .out(pla_5_out));
  assign bit_extender_1_out = {{34{onoff}}, onoff};  // Bit_Extender bit_extender_1
  assign {line5, line4, line3, line2, line1} = bit_extender_1_out & {pla_5_out, pla_4_out, pla_3_out, pla_2_out, pla_1_out};  // AND_Gate and_1, 35 bits wide
endmodule

module soundTrack1 (
  input  Stop,
  input  reset,
  output [7:0] out_3
);

  wire not_1_out, Track1_clock_out;
  wire [7:0] counter_1_q;

  Clock Track1_clock (.out(Track1_clock_out));
  not not_1 (not_1_out, Stop);
  Counter counter_1 (
    .count(not_1_out), .Q(counter_1_q), .clk(Track1_clock_out), .clr(reset));  // open: load, D, carry, up
  ROM Track01 (.addr(counter_1_q), .data(out_3));

  // Notes on the sheet:
  //   contents of Track01 (hex, n*v repeats v):
  //   80 80 3d 3d 3e 3e 40 40 39 39 42 42 4*80 42 42 40 40 3e 3e 3d 3d 3e 3e 40 40 6*80 3d 3d 40 80 40 40
  //   42 80 42 42 4*80 39 39 40 40 3d 40 40 42 42 3d 3d 3d 6*80 3d 3d 3e 3e 40 40 39 39 42 42 4*80 42 42
  //   44 44 3d 3d 3b 3b 3d 3d 45 45 45 80 80 80 45 80 45 45 44 44 42 42 40 40 42 80 42 80 42 80 40 80 40
  //   80 42 42 80 80 40 42 42 43 43 42 42 40 80 40 40 40 3e 3e 3d 3d 3e 3e 80 80 3e 3e 3d 3d 39 39 38 80
  //   38 38 39 39 3b 3b 3d 3d 3e 3e 3d 3d 3b 3b 80 3d 3d 80 39 39 80 80 39 80 39 80 39 39 3b 3b 39 39 3b
  //   3b 3d 3d 8*80 32 32 36 36 39 39 38 80 38 38 39 39 3b 3b 3d 3d 3e 3e 3d 3d 3b 3b 80 3d 3d 80 39 39 80
  //   80 39 80 39 80 39 39 3b 3b 39 39 3b 80 3b 3b 39 39 18*80
endmodule

module soundTrack2 (
  input  Stop,
  input  reset,
  output [7:0] out_3
);

  wire not_1_out, Track02_clock_out;
  wire [7:0] counter_1_q;

  Clock Track02_clock (.out(Track02_clock_out));
  Counter counter_1 (
    .count(not_1_out), .Q(counter_1_q), .clk(Track02_clock_out), .clr(reset));  // open: load, D, carry, up
  not not_1 (not_1_out, Stop);
  ROM Track02 (.addr(counter_1_q), .data(out_3));
  // sound_emitter sound_emitter_1: pin names not known; wires that end beside it: out_3

  // Notes on the sheet:
  //   contents of Track02 (hex, n*v repeats v):
  //   80 80 43 43 41 41 4*40 4*48 6*47 4a 4a 4*48 4*80 45 45 48 48 4c 4c 4d 4c 4c 4a 4a 4a 48 48 48 80 80
  //   80 45 45 48 48 4c 4c 48 80 48 48 4c 4c 4a 4a 4a 80 80 80 43 43 41 41 4*40 4*48 6*47 4a 4a 48 48 47
  //   47 45 45 45 5*80 45 45 48 48 4c 4c 4d 4c 4c 4a 4a 4a 48 48 48 80 80 80 45 45 48 48 4c 4c 48 80 48 48
  //   4c 4c 4*4a 48 80 6*48 6*80 43 43 41 41 4*40 4*48 6*47 4a 4a 4*48 4*80 45 45 48 48 4c 4c 4d 4d 4c 4a
  //   4a 4a 48 48 48 80 80 45 45 48 48 4c 4c 48 80 48 48 4c 4c 4a 4a 80 80 43 43 41 41 4*40 4*48 5*47 4a
  //   4a 48 48 47 47 45 45 45 80 80 80 45 45 48 48 4c 4c 4d 4c 4c 4a 4a 48 80 48 48 5*80
endmodule

module soundTrack3 (
  input  stop,
  input  reset,
  output [7:0] out_3
);

  wire not_1_out, Track03_clock_out;
  wire [7:0] counter_1_q;

  Clock Track03_clock (.out(Track03_clock_out));
  not not_1 (not_1_out, stop);
  ROM Track03 (.addr(counter_1_q), .data(out_3));
  Counter counter_1 (
    .count(not_1_out), .Q(counter_1_q), .clk(Track03_clock_out), .clr(reset));  // open: load, D, carry, up

  // Notes on the sheet:
  //   contents of Track03 (hex, n*v repeats v):
  //   80 80 3b 80 3b 3b 43 43 42 42 43 43 42 43 43 43 42 42 40 40 3e 3e 40 40 47 80 47 47 80 80 80 42 42
  //   43 45 45 42 42 40 40 3e 80 4*3e 4*80 3b 3c 3e 80 3e 3e 3c 80 3c 3c 40 3e 3e 3b 39 37 80 34 37 37 3e
  //   3e 3c 80 3c 3c 40 80 40 40 3f 3f 40 40 42 42 43 43 42 42 43 43 42 43 43 43 42 42 40 40 3e 3e 40 40
  //   47 80 47 47 47 80 80 42 42 43 45 45 42 42 40 40 3e 80 3e 3e 45 45 43 43 80 80 3b 3c 3e 80 3e 3e 3c
  //   80 3c 3c 40 3e 80 37 80 37 37 80 34 37 3e 3e 3c 80 3c 3c 40 3e 3e 43 80 43 43 43 37 39 3c 3c 3b 3b
  //   3c 3c 3e 3e 4*3b 6*39 80 80 80 40 40 42 8*43 4*80 3b 3b 3e 80 3e 3e 8*3c 80 80 80 40 40 43 8*42 80
  //   80 80 40 40 42 8*43 4a 4a 43 43 43 7*80
endmodule

module recoding (
  input  reset,
  input  stop,
  input  start_recoding,
  input  listen,
  input  [7:0] piano,
  output [7:0] out_6,
  output mode_listening,
  output mode_recoding
);

  wire and_1_out, clock_1_out, not_1_out, or_1_out, recoding_clock_out, xor_1_out;
  wire [7:0] counter_1_q;

  Clock recoding_clock (.out(recoding_clock_out));
  not not_1 (not_1_out, stop);
  T_Flip_Flop t_ff_1 (.T(not_1_out), .clk(start_recoding), .Q(mode_recoding));  // open: Qn, reset, preset
  T_Flip_Flop t_ff_2 (.T(not_1_out), .clk(listen), .Q(mode_listening));  // open: Qn, reset, preset
  or or_1 (or_1_out, reset, listen);
  xor xor_1 (xor_1_out, mode_recoding, mode_listening);
  Counter counter_1 (.clr(or_1_out), .count(not_1_out), .clk(and_1_out), .Q(counter_1_q));  // open: load, up, D, carry
  and and_1 (and_1_out, recoding_clock_out, xor_1_out);
  RAM ram_1 (.addr(counter_1_q), .we(mode_recoding), .oe(mode_listening), .clk(clock_1_out), .din(piano), .dout(out_6));
  Clock clock_1 (.out(clock_1_out));
endmodule
